# Fritzing sketch sensors simple (saved by Fritzing 0.8.5b)
breadboards: 1

parts:
  Part1 = Spark Core (v1.0)
  T1 = LM35 Temperature Sensor [package="TO92 [THT]"]
  LED1 = RGB LED (com. anode, rbg) [package="5 mm [THT]"]
  R1 = Resistor [tolerance=±5% resistance=220 package=THT]
  R2 = Resistor [tolerance=±5% resistance=220 package=THT]
  R3 = Resistor [tolerance=±5% resistance=220 package=THT]
  R4 = Photocell (LDR) [package=THT]
  R5 = Photocell (LDR) [package=THT]
  R6 = Resistor [tolerance=±5% resistance=10k package=THT]
  C1 = Ceramic Capacitor [capacitance=10nF package="100 mil [THT, multilayer]"]

nets:
  N1: Part1.A0, R2.Pin_1
  N2: Part1.A1, R1.Pin_1
  N3: Part1.A3, T1.Vout, C1.0
  N4: Part1.A5, R6.Pin_1
  GND: Part1.GND, T1.GND, LED1.common_anode, C1.1
  N5: Part1.3V3*, T1.+Vs, R5.pin_1
  N6: LED1.red_cathode, R1.Pin_0
  N7: LED1.blue_cathode, R2.Pin_0
  N8: LED1.green_cathode, R3.Pin_0
  N9: R4.pin_0, R6.Pin_0
  N10: R4.pin_1, R5.pin_0
